# Fritzing sketch 16 Fader (saved by Fritzing 0.9.4)
circuit board: 8.46667cm x 5.64444cm
breadboards: 1

parts:
  SparkFun_ESP32_Thing1 = SparkFun ESP32 Thing [part_number=DEV-13907]
  U2 = POT [package=alps_pot]
  U3 = POT [package=alps_pot]
  U4 = POT [package=alps_pot]
  U5 = POT [package=alps_pot]
  U6 = POT [package=alps_pot]
  U7 = POT [package=alps_pot]
  U8 = POT [package=alps_pot]
  U9 = POT [package=alps_pot]
  U10 = POT [package=alps_pot]
  U11 = POT [package=alps_pot]
  U12 = POT [package=alps_pot]
  U13 = POT [package=alps_pot]
  U14 = POT [package=alps_pot]
  U15 = POT [package=alps_pot]
  U16 = POT [package=alps_pot]
  U17 = POT [package=alps_pot]

nets:
  N1: SparkFun_ESP32_Thing1.14, U4.S
  N2: SparkFun_ESP32_Thing1.27, U5.S
  N3: SparkFun_ESP32_Thing1.26, U6.S
  N4: SparkFun_ESP32_Thing1.25, U7.S
  N5: SparkFun_ESP32_Thing1.35, U8.S
  N6: SparkFun_ESP32_Thing1.34, U9.S
  N7: SparkFun_ESP32_Thing1.32K_XN, U10.S
  N8: SparkFun_ESP32_Thing1.32K_XP, U11.S
  N9: SparkFun_ESP32_Thing1.39, U12.S
  N10: SparkFun_ESP32_Thing1.38, U13.S
  N11: SparkFun_ESP32_Thing1.37, U14.S
  N12: SparkFun_ESP32_Thing1.36, U15.S
  N13: SparkFun_ESP32_Thing1.GND, U10.A, U11.A, U12.A, U13.A, U14.A, U15.A, U16.A, U17.A
  N14: SparkFun_ESP32_Thing1.3.3V, U10.E, U11.E, U12.E, U13.E, U14.E, U15.E, U16.E, U17.E
  N15: SparkFun_ESP32_Thing1.4, U16.S
  N16: SparkFun_ESP32_Thing1.15, U17.S
  N17: U2.E, U3.E, U4.E, U5.E, U6.E, U7.E, U8.E, U9.E
  N18: U2.A, U3.A, U4.A, U5.A, U6.A, U7.A, U8.A, U9.A

custom parts:
  SparkFun ESP32 Thing: The SparkFun ESP32 Thing is a comprehensive development platform for Espressif’s ESP32, their super-charged version of the popular ESP8266. Like the 8266, the ESP32 is a WiFi-compatible microcontroller, but to that it adds support for Bluetooth low-energy (i.e BLE, BT4.0, Bluetooth Smart), and nearly 30 I/O pins. The ESP32’s power and versatility will make it the foundation of IoT and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
