# Fritzing sketch 5 Fader (saved by Fritzing 0.9.4)
breadboards: 1

parts:
  SparkFun_ESP32_Thing1 = SparkFun ESP32 Thing [part_number=DEV-13907]
  U2 = POT [package=alps_pot]
  U3 = POT [package=alps_pot]
  U4 = POT [package=alps_pot]
  U5 = POT [package=alps_pot]
  U6 = POT [package=alps_pot]

nets:
  N1: SparkFun_ESP32_Thing1.14, U4.S
  N2: SparkFun_ESP32_Thing1.27, U5.S
  N3: SparkFun_ESP32_Thing1.26, U6.S
  N4: U2.E, U3.E, U4.E, U5.E, U6.E
  N5: U2.A, U3.A, U4.A, U5.A, U6.A

custom parts:
  SparkFun ESP32 Thing: The SparkFun ESP32 Thing is a comprehensive development platform for Espressif’s ESP32, their super-charged version of the popular ESP8266. Like the 8266, the ESP32 is a WiFi-compatible microcontroller, but to that it adds support for Bluetooth low-energy (i.e BLE, BT4.0, Bluetooth Smart), and nearly 30 I/O pins. The ESP32’s power and versatility will make it the foundation of IoT and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
